# Fritzing sketch PumpController-ArduinoStack (saved by Fritzing 0.9.3b)

parts:
  Part1 = Arduino Uno (Rev3)
  Part2 = Arduino Xbee Libellium Shield
  Part3 = JeePlug experimenter's board
  Part4 = JeePlug experimenter's board
  Part5 = JeePlug experimenter's board
  Part6 = JeePlug experimenter's board
  Part7 = JeePlug experimenter's board
  Part8 = JeePlug experimenter's board
  Part9 = NCP1400 Step-Up Breakout
  LTR_1 = Monacor line transformer [part_number=LTR-110]
  J18 = Camdenboss CTB0158-3 [part_number=CTB0158-3 package=THT]
  J19 = Camdenboss CTB0158-3 [part_number=CTB0158-3 package=THT]
  J21 = Camdenboss CTB0158-4 [part_number=CTB0158-4 package=THT]
  J22 = Camdenboss CTB0158-4 [part_number=CTB0158-4 package=THT]
  J25 = Camdenboss CTB0158-4 [part_number=CTB0158-4 package=THT]
  J26 = Camdenboss CTB0158-4 [part_number=CTB0158-4 package=THT]
  J27 = female pin header, 2 pins [form="♀ (female)"]
  Power_plug1 = Power plug
  U6 = RELAY-SOLIDSTATE [package=relay-s108t02]
  RELAY2 = CAR RELAY [part_number=NVF4-2 package=THT]
  S6 = Taiway 100-SP-X-T1 SPDT Miniature Toggle Switch [part_number=100-SP-X-T1-0-0-B1-M2 package=THT]
  S7 = Round Pushbutton
  S8 = SPST Switch [package=switch-spdt_lock.007s]
  F1 = Resettable Fuse PTC [package=ptc]
  F2 = Resettable Fuse PTC [package=ptc]
  F3 = Resettable Fuse PTC [package=ptc]
  RELAY3 = CAR RELAY [part_number=NVF4-2 package=THT]
  RELAY4 = CAR RELAY [part_number=NVF4-2 package=THT]
  M1 = DC Motor  # not connected
  JP2 = Header 4 [package=molex-1x4_lock]
  JP3 = Header 4 [package=1x04-smd]

nets:
  N1: Part1.A0, Part2.A0, Part5.N$24, Part5.N$48, J18.pin3
  N2: Part1.A1, Part2.A1, Part5.A1, Part5.N$50, J18.pin2
  N3: Part1.A2, Part2.A2, Part5.A2, Part5.N$52, J18.pin1
  N4: Part1.A3, Part2.A3, Part5.A3, Part5.N$53, J19.pin3
  N5: Part1.A4/SDA, Part2.A4, Part4.N$48, Part5.A4, J19.pin2
  N6: Part1.A5/SCL, Part2.A5, Part4.N$50, Part5.A5, J19.pin1
  N7: Part1.D0/RX, Part2.M8RXD
  N8: Part1.D1/TX, Part2.M8TXD
  N9: Part1.D2, Part2.D2, Part2.2, Part6.B2, Part6.N$16
  N10: Part1.D3_PWM, Part2.D3, Part2.DOUT, Part6.B3, Part6.N$25
  N11: Part1.D4, Part2.D4, Part6.B4, Part6.N$18, J22.pin1, J25.pin1
  N12: Part1.D5_PWM, Part2.D5, Part6.B5, Part6.N$20, J22.pin2, J25.pin2
  N13: Part1.D6_PWM, Part2.D6, Part6.B6, Part6.N$21, J22.pin3, J25.pin3
  N14: Part1.D7, Part2.D7, Part6.N$8, Part7.N$16, J22.pin4, J25.pin4
  N15: Part2.GND, Part3.A5, Part3.N$30, Part3.N$44, Part5.N$16, Part8.A5, J26.pin1, J26.pin2, J26.pin3, J26.pin4
  N16: Part2.+5V, Part6.A1, Part8.B5, Part8.N$14, Part8.N$30, Part8.N$44, J21.pin1, J21.pin2, J21.pin3, J21.pin4
  N17: Part6.A2, J27.pin1
  N18: Part6.A3, J27.pin2
  GND: Part9.GND, LTR_1.GND, U6.-, JP3.3
  N19: Part9.VOUT, JP3.4
  N20: Part9.VIN, LTR_1.02
  N21: LTR_1.01, S6.COM, F1.1, RELAY4.85
  N22: LTR_1.08, F2.1, RELAY3.85
  N23: LTR_1.07, RELAY2.85, F3.1
  N24: J22.terminal_3, JP2.3
  N25: J22.terminal_4, JP2.4
  N26: Power_plug1.VCC, JP2.1
  N27: Power_plug1.GND, JP2.2
  N28: U6.T2, S6.L1
  N29: U6.+, JP3.1
  N30: S6.L2, S7.leg1, S8.O, S8.P
  N31: S7.leg0, S8.S

notes:
  Vdc Plug
  Fulree 3005ADJ DC/DC Convertor
  RHINO 480VAC 3-phase Power Supply
  24Vdc
  D2-D7
  RX/TX -> D2/D3
  Power
  Analog A5-A0
  D4-D7
  A5-A0
  7Vdc to 12Vdc
  SSR
  Start Button
  Hand
  Auto
  L1
  L2
  L3
  Contactor - Starter
  Pump
  Aux
  MAIN BREAKER DISCONNECT
  4-PIN (RED,BLK,BLK,YEL)
  PC Power Plug
  EXIT PLUG
